// Logisim project control.circ as structural Verilog: 1 circuit, main circuit main
module main (
  input  start,
  input  lsb,
  input  clck,
  input  countereq,
  input  reset,
  output clear_reg,
  output clear_counter,
  output _0mux_product,
  output mux_multiplier,
  output _1mux_product,
  output inc_counter,
  output enable_register,
  output rightshift
);

  wire and_1_out, and_2_out, and_3_out, and_4_out, and_5_out, and_6_out, and_7_out, and_8_out, and_9_out,
       and_10_out, and_11_out, and_12_out, and_13_out, and_14_out, and_15_out, and_16_out, not_1_out,
       not_2_out, not_3_out, not_4_out, not_5_out, not_6_out, not_7_out, not_8_out, not_9_out, not_10_out;
  wire [2:0] n0_out, register_1_q;

  Register #(.width(3)) register_1 (.D(n0_out), .en(1'b1), .Q(register_1_q), .clk(clck));  // open: clr
  not not_1 (not_1_out, register_1_q[0]);
  not not_2 (not_2_out, register_1_q[1]);
  not not_3 (not_3_out, register_1_q[2]);
  not not_4 (not_4_out, start);
  not not_5 (not_5_out, lsb);
  not not_6 (not_6_out, countereq);
  not not_7 (not_7_out, reset);
  and and_1 (and_1_out, not_3_out, register_1_q[1], not_1_out, not_5_out);
  and and_2 (and_2_out, not_3_out, register_1_q[1], register_1_q[0]);
  and and_3 (and_3_out, register_1_q[2], not_2_out, not_1_out);
  and and_4 (and_4_out, countereq, register_1_q[0], register_1_q[2], not_2_out);
  and and_5 (and_5_out, register_1_q[2], register_1_q[1], not_7_out, register_1_q[0]);
  and and_6 (and_6_out, register_1_q[0], not_2_out, not_3_out);
  and and_7 (and_7_out, not_1_out, register_1_q[1], not_3_out, lsb);
  and and_8 (and_8_out, countereq, register_1_q[0], register_1_q[2], not_2_out);
  and and_9 (and_9_out, register_1_q[2], register_1_q[1], not_7_out, register_1_q[0]);
  and and_10 (and_10_out, not_1_out, not_2_out, not_3_out, start);
  and and_11 (and_11_out, register_1_q[1], not_1_out, not_3_out, lsb);
  and and_12 (and_12_out, not_1_out, not_2_out, register_1_q[2]);
  and and_13 (and_13_out, register_1_q[0], not_2_out, register_1_q[2], not_6_out);
  and and_14 (and_14_out, register_1_q[0], register_1_q[2], not_2_out, countereq);
  and and_15 (and_15_out, register_1_q[0], register_1_q[1], register_1_q[2], not_7_out);
  and and_16 (and_16_out, register_1_q[0], register_1_q[2], not_2_out, not_6_out);
  or n2 (n0_out[2], and_1_out, and_2_out, and_3_out, and_4_out, and_5_out);
  or n1 (n0_out[1], and_6_out, and_7_out, and_16_out, and_8_out, and_9_out);
  or n0 (n0_out[0], and_10_out, and_11_out, and_12_out, and_14_out, and_15_out);
  not not_8 (not_8_out, not_2_out);
  not not_9 (not_9_out, not_3_out);
  not not_10 (not_10_out, not_1_out);
  and s0 (clear_counter, not_3_out, not_2_out, not_1_out);
  and s1 (_0mux_product, not_3_out, not_2_out, not_10_out);
  and s3 (_1mux_product, not_3_out, not_8_out, not_10_out);
  and s4 (inc_counter, not_9_out, not_1_out, not_2_out);
  or or_1 (enable_register, _0mux_product, _1mux_product, inc_counter);
  // OR_Gate or_2 has open pins: in0=inc_counter, in1=_1mux_product, out=open

  assign clear_reg = clear_counter;
  assign mux_multiplier = _0mux_product;
  assign rightshift = inc_counter;
endmodule
