// Logisim project datapath.circ as structural Verilog: 4 circuits, main circuit Main
module main (
  input  shiftvalue,
  input  rigth_shift,
  input  [31:0] Product_half,
  input  [31:0] multiplier,
  input  [1:0] mux_product,
  input  mux_multiplier,
  input  enable_reg,
  input  clear_reg,
  input  clck,
  input  [31:0] multiplicand_product,
  output lsb,
  output [31:0] out_productright,
  output [31:0] out_productleft
);

  wire [31:0] multiplexer_22_out, multiplexer_33_out, multiplexer_35_out, multiplexer_66_out;

  Multiplexer #(.enable("false")) multiplexer_1 (
    .in0(out_productleft[31]), .in1(shiftvalue), .out(multiplexer_35_out[31]), .sel(rigth_shift));
  Multiplexer #(.enable("false")) multiplexer_2 (
    .in0(out_productleft[30]), .in1(out_productleft[31]), .out(multiplexer_35_out[30]), .sel(rigth_shift));
  Multiplexer #(.enable("false")) multiplexer_3 (
    .in0(out_productleft[29]), .in1(out_productleft[30]), .out(multiplexer_35_out[29]), .sel(rigth_shift));
  Multiplexer #(.enable("false")) multiplexer_4 (
    .in0(out_productleft[27]), .in1(out_productleft[28]), .out(multiplexer_35_out[27]), .sel(rigth_shift));
  Multiplexer #(.enable("false")) multiplexer_5 (
    .in0(out_productleft[28]), .in1(out_productleft[29]), .out(multiplexer_35_out[28]), .sel(rigth_shift));
  Multiplexer #(.enable("false")) multiplexer_6 (
    .in0(out_productleft[26]), .in1(out_productleft[27]), .out(multiplexer_35_out[26]), .sel(rigth_shift));
  Multiplexer #(.enable("false")) multiplexer_7 (
    .in0(out_productleft[25]), .in1(out_productleft[26]), .out(multiplexer_35_out[25]), .sel(rigth_shift));
  Multiplexer #(.enable("false")) multiplexer_8 (
    .in0(out_productleft[24]), .in1(out_productleft[25]), .out(multiplexer_35_out[24]), .sel(rigth_shift));
  Multiplexer #(.enable("false")) multiplexer_9 (
    .in0(out_productleft[23]), .in1(out_productleft[24]), .out(multiplexer_35_out[23]), .sel(rigth_shift));
  Multiplexer #(.enable("false")) multiplexer_10 (
    .in0(out_productleft[21]), .in1(out_productleft[22]), .out(multiplexer_35_out[21]), .sel(rigth_shift));
  Multiplexer #(.enable("false")) multiplexer_11 (
    .in0(out_productleft[22]), .in1(out_productleft[23]), .out(multiplexer_35_out[22]), .sel(rigth_shift));
  Multiplexer #(.enable("false")) multiplexer_12 (
    .in0(out_productleft[19]), .in1(out_productleft[20]), .out(multiplexer_35_out[19]), .sel(rigth_shift));
  Multiplexer #(.enable("false")) multiplexer_13 (
    .in0(out_productleft[20]), .in1(out_productleft[21]), .out(multiplexer_35_out[20]), .sel(rigth_shift));
  Multiplexer #(.enable("false")) multiplexer_14 (
    .in0(out_productleft[17]), .in1(out_productleft[18]), .out(multiplexer_35_out[17]), .sel(rigth_shift));
  Multiplexer #(.enable("false")) multiplexer_15 (
    .in0(out_productleft[18]), .in1(out_productleft[19]), .out(multiplexer_35_out[18]), .sel(rigth_shift));
  Multiplexer #(.enable("false")) multiplexer_16 (
    .in0(out_productleft[15]), .in1(out_productleft[16]), .out(multiplexer_35_out[15]), .sel(rigth_shift));
  Multiplexer #(.enable("false")) multiplexer_17 (
    .in0(out_productleft[16]), .in1(out_productleft[17]), .out(multiplexer_35_out[16]), .sel(rigth_shift));
  Multiplexer #(.enable("false")) multiplexer_18 (
    .in0(out_productleft[13]), .in1(out_productleft[14]), .out(multiplexer_35_out[13]), .sel(rigth_shift));
  Multiplexer #(.enable("false")) multiplexer_19 (
    .in0(out_productleft[14]), .in1(out_productleft[15]), .out(multiplexer_35_out[14]), .sel(rigth_shift));
  Multiplexer #(.enable("false")) multiplexer_20 (
    .in0(out_productleft[12]), .in1(out_productleft[13]), .out(multiplexer_35_out[12]), .sel(rigth_shift));
  Multiplexer #(.enable("false")) multiplexer_21 (
    .in0(out_productleft[11]), .in1(out_productleft[12]), .out(multiplexer_35_out[11]), .sel(rigth_shift));
  Multiplexer #(.select(2), .width(32), .enable("false")) multiplexer_22 (
    .in0(multiplexer_35_out), .in1(Product_half), .in2(multiplicand_product), .out(multiplexer_22_out),
    .sel(mux_product));  // open: in3
  Multiplexer #(.enable("false")) multiplexer_23 (
    .in0(out_productleft[10]), .in1(out_productleft[11]), .out(multiplexer_35_out[10]), .sel(rigth_shift));
  Multiplexer #(.enable("false")) multiplexer_24 (
    .in0(out_productleft[9]), .in1(out_productleft[10]), .out(multiplexer_35_out[9]), .sel(rigth_shift));
  Multiplexer #(.enable("false")) multiplexer_25 (
    .in0(out_productleft[7]), .in1(out_productleft[8]), .out(multiplexer_35_out[7]), .sel(rigth_shift));
  Multiplexer #(.enable("false")) multiplexer_26 (
    .in0(out_productleft[8]), .in1(out_productleft[9]), .out(multiplexer_35_out[8]), .sel(rigth_shift));
  Multiplexer #(.enable("false")) multiplexer_27 (
    .in0(out_productleft[5]), .in1(out_productleft[6]), .out(multiplexer_35_out[5]), .sel(rigth_shift));
  Multiplexer #(.enable("false")) multiplexer_28 (
    .in0(out_productleft[6]), .in1(out_productleft[7]), .out(multiplexer_35_out[6]), .sel(rigth_shift));
  Multiplexer #(.enable("false")) multiplexer_29 (
    .in0(out_productleft[3]), .in1(out_productleft[4]), .out(multiplexer_35_out[3]), .sel(rigth_shift));
  Multiplexer #(.enable("false")) multiplexer_30 (
    .in0(out_productleft[4]), .in1(out_productleft[5]), .out(multiplexer_35_out[4]), .sel(rigth_shift));
  Register #(.width(32)) register_1 (
    .D(multiplexer_22_out), .en(enable_reg), .Q(out_productleft), .clk(clck), .clr(clear_reg));
  Multiplexer #(.enable("false")) multiplexer_31 (
    .in0(out_productleft[2]), .in1(out_productleft[3]), .out(multiplexer_35_out[2]), .sel(rigth_shift));
  Multiplexer #(.enable("false")) multiplexer_32 (
    .in0(out_productleft[1]), .in1(out_productleft[2]), .out(multiplexer_35_out[1]), .sel(rigth_shift));
  Multiplexer #(.width(32), .enable("false")) multiplexer_33 (
    .in0(multiplexer_66_out), .in1(multiplier), .out(multiplexer_33_out), .sel(mux_multiplier));
  Multiplexer #(.enable("false")) multiplexer_34 (
    .in0(out_productright[31]), .in1(out_productleft[0]), .out(multiplexer_66_out[31]), .sel(rigth_shift));
  Multiplexer #(.enable("false")) multiplexer_35 (
    .in0(out_productleft[0]), .in1(out_productleft[1]), .out(multiplexer_35_out[0]), .sel(rigth_shift));
  Register #(.width(32)) register_2 (
    .D(multiplexer_33_out), .en(enable_reg), .Q({out_productright[31:1], lsb}), .clk(clck), .clr(clear_reg));
  Multiplexer #(.enable("false")) multiplexer_36 (
    .in0(out_productright[30]), .in1(out_productright[31]), .out(multiplexer_66_out[30]), .sel(rigth_shift));
  Multiplexer #(.enable("false")) multiplexer_37 (
    .in0(out_productright[29]), .in1(out_productright[30]), .out(multiplexer_66_out[29]), .sel(rigth_shift));
  Multiplexer #(.enable("false")) multiplexer_38 (
    .in0(out_productright[28]), .in1(out_productright[29]), .out(multiplexer_66_out[28]), .sel(rigth_shift));
  Multiplexer #(.enable("false")) multiplexer_39 (
    .in0(out_productright[27]), .in1(out_productright[28]), .out(multiplexer_66_out[27]), .sel(rigth_shift));
  Multiplexer #(.enable("false")) multiplexer_40 (
    .in0(out_productright[25]), .in1(out_productright[26]), .out(multiplexer_66_out[25]), .sel(rigth_shift));
  Multiplexer #(.enable("false")) multiplexer_41 (
    .in0(out_productright[26]), .in1(out_productright[27]), .out(multiplexer_66_out[26]), .sel(rigth_shift));
  Multiplexer #(.enable("false")) multiplexer_42 (
    .in0(out_productright[23]), .in1(out_productright[24]), .out(multiplexer_66_out[23]), .sel(rigth_shift));
  Multiplexer #(.enable("false")) multiplexer_43 (
    .in0(out_productright[24]), .in1(out_productright[25]), .out(multiplexer_66_out[24]), .sel(rigth_shift));
  Multiplexer #(.enable("false")) multiplexer_44 (
    .in0(out_productright[21]), .in1(out_productright[22]), .out(multiplexer_66_out[21]), .sel(rigth_shift));
  Multiplexer #(.enable("false")) multiplexer_45 (
    .in0(out_productright[22]), .in1(out_productright[23]), .out(multiplexer_66_out[22]), .sel(rigth_shift));
  Multiplexer #(.enable("false")) multiplexer_46 (
    .in0(out_productright[20]), .in1(out_productright[21]), .out(multiplexer_66_out[20]), .sel(rigth_shift));
  Multiplexer #(.enable("false")) multiplexer_47 (
    .in0(out_productright[19]), .in1(out_productright[20]), .out(multiplexer_66_out[19]), .sel(rigth_shift));
  Multiplexer #(.enable("false")) multiplexer_48 (
    .in0(out_productright[18]), .in1(out_productright[19]), .out(multiplexer_66_out[18]), .sel(rigth_shift));
  Multiplexer #(.enable("false")) multiplexer_49 (
    .in0(out_productright[17]), .in1(out_productright[18]), .out(multiplexer_66_out[17]), .sel(rigth_shift));
  Multiplexer #(.enable("false")) multiplexer_50 (
    .in0(out_productright[15]), .in1(out_productright[16]), .out(multiplexer_66_out[15]), .sel(rigth_shift));
  Multiplexer #(.enable("false")) multiplexer_51 (
    .in0(out_productright[16]), .in1(out_productright[17]), .out(multiplexer_66_out[16]), .sel(rigth_shift));
  Multiplexer #(.enable("false")) multiplexer_52 (
    .in0(out_productright[13]), .in1(out_productright[14]), .out(multiplexer_66_out[13]), .sel(rigth_shift));
  Multiplexer #(.enable("false")) multiplexer_53 (
    .in0(out_productright[14]), .in1(out_productright[15]), .out(multiplexer_66_out[14]), .sel(rigth_shift));
  Multiplexer #(.enable("false")) multiplexer_54 (
    .in0(out_productright[12]), .in1(out_productright[13]), .out(multiplexer_66_out[12]), .sel(rigth_shift));
  Multiplexer #(.enable("false")) multiplexer_55 (
    .in0(out_productright[11]), .in1(out_productright[12]), .out(multiplexer_66_out[11]), .sel(rigth_shift));
  Multiplexer #(.enable("false")) multiplexer_56 (
    .in0(out_productright[10]), .in1(out_productright[11]), .out(multiplexer_66_out[10]), .sel(rigth_shift));
  Multiplexer #(.enable("false")) multiplexer_57 (
    .in0(out_productright[9]), .in1(out_productright[10]), .out(multiplexer_66_out[9]), .sel(rigth_shift));
  Multiplexer #(.enable("false")) multiplexer_58 (
    .in0(out_productright[8]), .in1(out_productright[9]), .out(multiplexer_66_out[8]), .sel(rigth_shift));
  Multiplexer #(.enable("false")) multiplexer_59 (
    .in0(out_productright[7]), .in1(out_productright[8]), .out(multiplexer_66_out[7]), .sel(rigth_shift));
  Multiplexer #(.enable("false")) multiplexer_60 (
    .in0(out_productright[5]), .in1(out_productright[6]), .out(multiplexer_66_out[5]), .sel(rigth_shift));
  Multiplexer #(.enable("false")) multiplexer_61 (
    .in0(out_productright[6]), .in1(out_productright[7]), .out(multiplexer_66_out[6]), .sel(rigth_shift));
  Multiplexer #(.enable("false")) multiplexer_62 (
    .in0(out_productright[3]), .in1(out_productright[4]), .out(multiplexer_66_out[3]), .sel(rigth_shift));
  Multiplexer #(.enable("false")) multiplexer_63 (
    .in0(out_productright[4]), .in1(out_productright[5]), .out(multiplexer_66_out[4]), .sel(rigth_shift));
  Multiplexer #(.enable("false")) multiplexer_64 (
    .in0(out_productright[2]), .in1(out_productright[3]), .out(multiplexer_66_out[2]), .sel(rigth_shift));
  Multiplexer #(.enable("false")) multiplexer_65 (
    .in0(out_productright[1]), .in1(out_productright[2]), .out(multiplexer_66_out[1]), .sel(rigth_shift));
  Multiplexer #(.enable("false")) multiplexer_66 (
    .in0(lsb), .in1(out_productright[1]), .out(multiplexer_66_out[0]), .sel(rigth_shift));

  assign out_productright[0] = lsb;
endmodule

module _1_bitAdder (
  input  a_i,
  input  b_i,
  input  c_i,
  output c_i_1,
  output result
);

  wire and_1_out, and_2_out, and_3_out, not_1_out, not_2_out, or_2_out, or_3_out;

  or or_1 (c_i_1, and_1_out, and_3_out);
  and and_1 (and_1_out, b_i, a_i);
  not not_1 (not_1_out, and_1_out);
  and and_2 (and_2_out, not_1_out, or_2_out);
  and and_3 (and_3_out, and_2_out, c_i);
  not not_2 (not_2_out, and_3_out);
  and and_4 (result, not_2_out, or_3_out);
  or or_2 (or_2_out, a_i, b_i);
  or or_3 (or_3_out, and_2_out, c_i);
endmodule

module _32_bitAdder (
  input  [31:0] a_i32,
  input  [31:0] b_i32,
  input  c_i,
  output c_o,
  output [31:0] add_result
);

  wire n1_bitadder_2_c_i_1, n1_bitadder_3_c_i_1, n1_bitadder_4_c_i_1, n1_bitadder_5_c_i_1,
       n1_bitadder_6_c_i_1, n1_bitadder_7_c_i_1, n1_bitadder_8_c_i_1, n1_bitadder_9_c_i_1,
       n1_bitadder_10_c_i_1, n1_bitadder_11_c_i_1, n1_bitadder_12_c_i_1, n1_bitadder_13_c_i_1,
       n1_bitadder_14_c_i_1, n1_bitadder_15_c_i_1, n1_bitadder_16_c_i_1, n1_bitadder_17_c_i_1,
       n1_bitadder_18_c_i_1, n1_bitadder_19_c_i_1, n1_bitadder_20_c_i_1, n1_bitadder_21_c_i_1,
       n1_bitadder_22_c_i_1, n1_bitadder_23_c_i_1, n1_bitadder_24_c_i_1, n1_bitadder_25_c_i_1,
       n1_bitadder_26_c_i_1, n1_bitadder_27_c_i_1, n1_bitadder_28_c_i_1, n1_bitadder_29_c_i_1,
       n1_bitadder_30_c_i_1, n1_bitadder_31_c_i_1, n1_bitadder_32_c_i_1;

  _1_bitAdder u_1_bitadder_1 (
    .a_i(a_i32[31]), .c_i_1(c_o), .c_i(n1_bitadder_3_c_i_1), .b_i(b_i32[31]), .result(add_result[31]));
  _1_bitAdder u_1_bitadder_2 (
    .a_i(a_i32[29]), .c_i_1(n1_bitadder_2_c_i_1), .c_i(n1_bitadder_4_c_i_1), .b_i(b_i32[29]),
    .result(add_result[29]));
  _1_bitAdder u_1_bitadder_3 (
    .a_i(a_i32[30]), .c_i_1(n1_bitadder_3_c_i_1), .c_i(n1_bitadder_2_c_i_1), .b_i(b_i32[30]),
    .result(add_result[30]));
  _1_bitAdder u_1_bitadder_4 (
    .a_i(a_i32[28]), .c_i_1(n1_bitadder_4_c_i_1), .c_i(n1_bitadder_5_c_i_1), .b_i(b_i32[28]),
    .result(add_result[28]));
  _1_bitAdder u_1_bitadder_5 (
    .a_i(a_i32[27]), .c_i_1(n1_bitadder_5_c_i_1), .c_i(n1_bitadder_6_c_i_1), .b_i(b_i32[27]),
    .result(add_result[27]));
  _1_bitAdder u_1_bitadder_6 (
    .a_i(a_i32[26]), .c_i_1(n1_bitadder_6_c_i_1), .c_i(n1_bitadder_8_c_i_1), .b_i(b_i32[26]),
    .result(add_result[26]));
  _1_bitAdder u_1_bitadder_7 (
    .a_i(a_i32[24]), .c_i_1(n1_bitadder_7_c_i_1), .c_i(n1_bitadder_9_c_i_1), .b_i(b_i32[24]),
    .result(add_result[24]));
  _1_bitAdder u_1_bitadder_8 (
    .a_i(a_i32[25]), .c_i_1(n1_bitadder_8_c_i_1), .c_i(n1_bitadder_7_c_i_1), .b_i(b_i32[25]),
    .result(add_result[25]));
  _1_bitAdder u_1_bitadder_9 (
    .a_i(a_i32[23]), .c_i_1(n1_bitadder_9_c_i_1), .c_i(n1_bitadder_10_c_i_1), .b_i(b_i32[23]),
    .result(add_result[23]));
  _1_bitAdder u_1_bitadder_10 (
    .a_i(a_i32[22]), .c_i_1(n1_bitadder_10_c_i_1), .c_i(n1_bitadder_11_c_i_1), .b_i(b_i32[22]),
    .result(add_result[22]));
  _1_bitAdder u_1_bitadder_11 (
    .a_i(a_i32[21]), .c_i_1(n1_bitadder_11_c_i_1), .c_i(n1_bitadder_12_c_i_1), .b_i(b_i32[21]),
    .result(add_result[21]));
  _1_bitAdder u_1_bitadder_12 (
    .a_i(a_i32[20]), .c_i_1(n1_bitadder_12_c_i_1), .c_i(n1_bitadder_14_c_i_1), .b_i(b_i32[20]),
    .result(add_result[20]));
  _1_bitAdder u_1_bitadder_13 (
    .a_i(a_i32[18]), .c_i_1(n1_bitadder_13_c_i_1), .c_i(n1_bitadder_16_c_i_1), .b_i(b_i32[18]),
    .result(add_result[18]));
  _1_bitAdder u_1_bitadder_14 (
    .a_i(a_i32[19]), .c_i_1(n1_bitadder_14_c_i_1), .c_i(n1_bitadder_13_c_i_1), .b_i(b_i32[19]),
    .result(add_result[19]));
  _1_bitAdder u_1_bitadder_15 (
    .a_i(a_i32[16]), .c_i_1(n1_bitadder_15_c_i_1), .c_i(n1_bitadder_17_c_i_1), .b_i(b_i32[16]),
    .result(add_result[16]));
  _1_bitAdder u_1_bitadder_16 (
    .a_i(a_i32[17]), .c_i_1(n1_bitadder_16_c_i_1), .c_i(n1_bitadder_15_c_i_1), .b_i(b_i32[17]),
    .result(add_result[17]));
  _1_bitAdder u_1_bitadder_17 (
    .a_i(a_i32[15]), .c_i_1(n1_bitadder_17_c_i_1), .c_i(n1_bitadder_19_c_i_1), .b_i(b_i32[15]),
    .result(add_result[15]));
  _1_bitAdder u_1_bitadder_18 (
    .a_i(a_i32[13]), .c_i_1(n1_bitadder_18_c_i_1), .c_i(n1_bitadder_20_c_i_1), .b_i(b_i32[13]),
    .result(add_result[13]));
  _1_bitAdder u_1_bitadder_19 (
    .a_i(a_i32[14]), .c_i_1(n1_bitadder_19_c_i_1), .c_i(n1_bitadder_18_c_i_1), .b_i(b_i32[14]),
    .result(add_result[14]));
  _1_bitAdder u_1_bitadder_20 (
    .a_i(a_i32[12]), .c_i_1(n1_bitadder_20_c_i_1), .c_i(n1_bitadder_22_c_i_1), .b_i(b_i32[12]),
    .result(add_result[12]));
  _1_bitAdder u_1_bitadder_21 (
    .a_i(a_i32[10]), .c_i_1(n1_bitadder_21_c_i_1), .c_i(n1_bitadder_23_c_i_1), .b_i(b_i32[10]),
    .result(add_result[10]));
  _1_bitAdder u_1_bitadder_22 (
    .a_i(a_i32[11]), .c_i_1(n1_bitadder_22_c_i_1), .c_i(n1_bitadder_21_c_i_1), .b_i(b_i32[11]),
    .result(add_result[11]));
  _1_bitAdder u_1_bitadder_23 (
    .a_i(a_i32[9]), .c_i_1(n1_bitadder_23_c_i_1), .c_i(n1_bitadder_24_c_i_1), .b_i(b_i32[9]),
    .result(add_result[9]));
  _1_bitAdder u_1_bitadder_24 (
    .a_i(a_i32[8]), .c_i_1(n1_bitadder_24_c_i_1), .c_i(n1_bitadder_25_c_i_1), .b_i(b_i32[8]),
    .result(add_result[8]));
  _1_bitAdder u_1_bitadder_25 (
    .a_i(a_i32[7]), .c_i_1(n1_bitadder_25_c_i_1), .c_i(n1_bitadder_26_c_i_1), .b_i(b_i32[7]),
    .result(add_result[7]));
  _1_bitAdder u_1_bitadder_26 (
    .a_i(a_i32[6]), .c_i_1(n1_bitadder_26_c_i_1), .c_i(n1_bitadder_27_c_i_1), .b_i(b_i32[6]),
    .result(add_result[6]));
  _1_bitAdder u_1_bitadder_27 (
    .a_i(a_i32[5]), .c_i_1(n1_bitadder_27_c_i_1), .c_i(n1_bitadder_28_c_i_1), .b_i(b_i32[5]),
    .result(add_result[5]));
  _1_bitAdder u_1_bitadder_28 (
    .a_i(a_i32[4]), .c_i_1(n1_bitadder_28_c_i_1), .c_i(n1_bitadder_30_c_i_1), .b_i(b_i32[4]),
    .result(add_result[4]));
  _1_bitAdder u_1_bitadder_29 (
    .a_i(a_i32[2]), .c_i_1(n1_bitadder_29_c_i_1), .c_i(n1_bitadder_32_c_i_1), .b_i(b_i32[2]),
    .result(add_result[2]));
  _1_bitAdder u_1_bitadder_30 (
    .a_i(a_i32[3]), .c_i_1(n1_bitadder_30_c_i_1), .c_i(n1_bitadder_29_c_i_1), .b_i(b_i32[3]),
    .result(add_result[3]));
  _1_bitAdder u_1_bitadder_31 (
    .a_i(a_i32[0]), .c_i_1(n1_bitadder_31_c_i_1), .c_i(c_i), .b_i(b_i32[0]), .result(add_result[0]));
  _1_bitAdder u_1_bitadder_32 (
    .a_i(a_i32[1]), .c_i_1(n1_bitadder_32_c_i_1), .c_i(n1_bitadder_31_c_i_1), .b_i(b_i32[1]),
    .result(add_result[1]));
endmodule

module Main (
  input  [1:0] muxProductHalf,
  input  muxmultiplier,
  input  rightShiftEnable,
  input  [31:0] i_multiplicand,
  input  WriteEnableRegister,
  input  [31:0] i_ProductHalf,
  input  clearReg,
  input  clck,
  input  [31:0] i_multiplier,
  input  inc_counter,
  input  clearCounter,
  output lsb,
  output countereq,
  output [31:0] o_productleft,
  output [31:0] o_productlright
);

  wire and_1_out, and_2_out, n32_bitadder_1_c_o, not_1_out, not_2_out, register_1_q;
  wire [5:0] counter_1_q;
  wire [31:0] n32_bitadder_1_add_result;

  and and_1 (and_1_out, muxProductHalf[1], not_1_out);
  not not_1 (not_1_out, muxProductHalf[0]);
  and and_2 (and_2_out, not_2_out, and_1_out);
  not not_2 (not_2_out, muxmultiplier);
  Register #(.width(1)) register_1 (.D(n32_bitadder_1_c_o), .en(and_2_out), .Q(register_1_q), .clk(clck));  // open: clr
  main main_1 (
    .rigth_shift(rightShiftEnable), .mux_product(muxProductHalf), .mux_multiplier(muxmultiplier),
    .enable_reg(WriteEnableRegister), .clear_reg(clearReg), .clck(clck), .lsb(lsb),
    .Product_half(i_ProductHalf), .multiplier(i_multiplier),
    .multiplicand_product(n32_bitadder_1_add_result), .out_productleft(o_productleft),
    .shiftvalue(register_1_q), .out_productright(o_productlright));
  _32_bitAdder u_32_bitadder_1 (
    .b_i32(o_productleft), .c_o(n32_bitadder_1_c_o), .a_i32(i_multiplicand), .c_i(1'b0),
    .add_result(n32_bitadder_1_add_result));
  Counter #(.width(6), .max('h3f)) counter_1 (
    .Q(counter_1_q), .clk(inc_counter), .clr(clearCounter));  // open: load, D, count, carry
  Comparator #(.width(6)) comparator_1 (.a(counter_1_q), .b(6'b100000), .eq(countereq));  // open: gt, lt
endmodule
