// Logisim project mult32.circ as structural Verilog: 1 circuit, main circuit main
module main (
  input  [31:0] in_1,
  input  [31:0] in_2,
  output [31:0] out_3,
  output [31:0] out_4
);

  wire clock_1_out, main_1_countereq, main_1_lsb, main_2_clear_counter, main_2_clear_reg,
       main_2_enable_register, main_2_inc_counter, main_2_mux_multiplier, main_2_rightshift, reset_out,
       start_out;
  wire [1:0] main_2__0mux_product;

  Main main_1 (
    .muxProductHalf(main_2__0mux_product), .muxmultiplier(main_2_mux_multiplier),
    .rightShiftEnable(main_2_rightshift), .WriteEnableRegister(main_2_enable_register),
    .clearReg(main_2_clear_reg), .clck(clock_1_out), .inc_counter(main_2_inc_counter),
    .clearCounter(main_2_clear_counter), .lsb(main_1_lsb), .countereq(main_1_countereq),
    .i_multiplicand(in_2), .i_ProductHalf({32{1'b0}}), .i_multiplier(in_1), .o_productleft(out_3),
    .o_productlright(out_4));
  Button start (.out(start_out));
  Clock clock_1 (.out(clock_1_out));
  Button reset (.out(reset_out));
  control_main main_2 (
    .start(start_out), .lsb(main_1_lsb), .clck(clock_1_out), .countereq(main_1_countereq), .reset(reset_out),
    .clear_reg(main_2_clear_reg), .clear_counter(main_2_clear_counter),
    ._0mux_product(main_2__0mux_product[0]), .mux_multiplier(main_2_mux_multiplier),
    ._1mux_product(main_2__0mux_product[1]), .inc_counter(main_2_inc_counter),
    .enable_register(main_2_enable_register), .rightshift(main_2_rightshift));

  // Notes on the sheet:
  //   leftt part
  //   rigth part
  //   MULTIPLIER
  //   MULTIPLICAND
endmodule
